# Fritzing sketch lvSensor (saved by Fritzing 0.8.7b)
breadboards: 1

parts:
  부품1 = Arduino Uno (Rev3)
  T1 = LM35 Temperature Sensor [package="TO92 [THT]"]
  T2 = LM35 Temperature Sensor [package="TO92 [THT]"]
  LED1 = LED - 5mm [color="Yellow (595nm)" package="5 mm [THT]"]
  LED2 = LED - 5mm [color="Green (570nm)" package="5 mm [THT]"]
  R1 = Resistor [tolerance=±5% resistance=220 package=THT]
  R2 = Resistor [tolerance=±5% resistance=220 package=THT]

nets:
  N1: 부품1.A0, T2.Vout
  N2: 부품1.A4/SDA, T1.Vout
  N3: 부품1.D8, LED2.anode
  N4: 부품1.D9_PWM, LED1.anode
  N5: 부품1.5V, T1.+Vs, T2.+Vs
  GND: 부품1.GND, T1.GND, T2.GND, R1.Pin_0, R2.Pin_0
  N6: LED1.cathode, R1.Pin_1
  N7: LED2.cathode, R2.Pin_1
